# Fritzing sketch level-indicator (saved by Fritzing 0.9.2b)
breadboards: 3

parts:
  Part1 = Electric Imp April
  shif_out_controller = 74HC595 [package="DIP16 [THT]"]
  1088BS_LED_matrix = LBT2088AH [part_number=1088BS]
  R1 = Resistor [tolerance=±5% resistance=560 package="2010 [SMD]"]
  R2 = Resistor [tolerance=±5% resistance=560 package="2010 [SMD]"]
  R3 = Resistor [tolerance=±5% resistance=560 package="2010 [SMD]"]
  R4 = Resistor [tolerance=±5% resistance=560 package="2010 [SMD]"]
  R5 = Resistor [tolerance=±5% resistance=560 package="2010 [SMD]"]
  R6 = Resistor [tolerance=±5% resistance=560 package="2010 [SMD]"]
  R7 = Resistor [tolerance=±5% resistance=560 package="2010 [SMD]"]
  R8 = Resistor [tolerance=±5% resistance=560 package="2010 [SMD]"]

nets:
  N1: Part1.3, shif_out_controller.DS
  N2: Part1.5, shif_out_controller.ST_CP
  N3: Part1.6, shif_out_controller.SH_CP
  N4: Part1.8, shif_out_controller.MR, shif_out_controller.VCC
  N5: Part1.9, shif_out_controller.GND, shif_out_controller.OE, 1088BS_LED_matrix.pin2, 1088BS_LED_matrix.pin_3, 1088BS_LED_matrix.pin_5, 1088BS_LED_matrix.pin_7, 1088BS_LED_matrix.pin_8, 1088BS_LED_matrix.pin_11, 1088BS_LED_matrix.pin_12, 1088BS_LED_matrix.pin_14
  N6: shif_out_controller.Q1, R4.Pin_1
  N7: shif_out_controller.Q2, R2.Pin_0
  N8: shif_out_controller.Q3, R5.Pin_1
  N9: shif_out_controller.Q4, R6.Pin_0
  N10: shif_out_controller.Q5, R3.Pin_0
  N11: shif_out_controller.Q6, R8.Pin_1
  N12: shif_out_controller.Q7, R7.Pin_0
  N13: shif_out_controller.Q0, R1.Pin_0
  N14: 1088BS_LED_matrix.pin1, R7.Pin_1
  N15: 1088BS_LED_matrix.pin_4, R6.Pin_1
  N16: 1088BS_LED_matrix.pin_6, R8.Pin_0
  N17: 1088BS_LED_matrix.pin_9, R5.Pin_0
  N18: 1088BS_LED_matrix.pin_10, R4.Pin_0
  N19: 1088BS_LED_matrix.pin_13, R1.Pin_1
  N20: 1088BS_LED_matrix.pin_15, R2.Pin_1
  N21: 1088BS_LED_matrix.pin_16, R3.Pin_1

notes:
  pin5 : data out
  pin8 : latch
  pin9 : clock
  label side up
  groups of 4, top wire is closest to centre
  orange wires control rows, black ones columns

custom parts:
  Electric Imp April: Electric Imp Breakout Board with onboard 3.3V regulated power supply
