# Fritzing sketch light-and-beeping-schematic (saved by Fritzing 0.9.2b)
breadboards: 1

parts:
  Electric_IMP_April = Electric Imp April
  SG1 = Buzzer 12mm [package=buzzer-12mm]
  R1 = Resistor [tolerance=±5% resistance=220 package=THT]
  LED1 = RGB LED - (4 legs) [package="5 mm [THT]"]
  R2 = Resistor [tolerance=±5% resistance=220 package=THT]

nets:
  N1: Electric_IMP_April.4, SG1.1
  N2: Electric_IMP_April.5, R2.Pin_1
  N3: Electric_IMP_April.6, R1.Pin_1
  N4: Electric_IMP_April.11, SG1.2
  N5: R1.Pin_0, LED1.green_cathode
  N6: LED1.common_anode, R2.Pin_0

custom parts:
  Electric Imp April: Electric Imp Breakout Board with onboard 3.3V regulated power supply
